# Fritzing sketch schema (saved by Fritzing 0.9.2b)
circuit board: 10.3178cm x 5.69486cm
breadboards: 2

parts:
  RHT2 = Humidity and Temperature Sensor RHT03
  R3 = Resistor [tolerance=±5% resistance=220 package=THT]
  LED1 = Super Flux LED blue [color=Blue]
  RHT1 = Humidity and Temperature Sensor RHT03
  R4 = Resistor [tolerance=±5% resistance=220 package=THT]
  R5 = Resistor [tolerance=±5% resistance=220 package=THT]
  Part1 = Arduino Nano (Rev3.0)
  Part2 = Real Time Clock Module - DS1307 RTC Breakout Board
  U2 = microSD Socket [package="Molex 502774-0891 [SMD]"]

nets:
  VCC: RHT2.Vcc, RHT1.Vcc, R4.Pin_1, R5.Pin_1, Part1.3V3
  N1: RHT2.Data-signal, R5.Pin_0, Part1.D3
  GND: RHT2.GND_2, LED1.cathode, RHT1.GND_2, Part1.GND, Part2.GND, U2.GND
  N2: R3.Pin_0, Part1.D8
  N3: R3.Pin_1, LED1.anode
  N4: RHT1.Data-signal, R4.Pin_0, Part1.D2
  N5: Part1.D10, U2.CS
  N6: Part1.D11/MOSI, U2.DI
  N7: Part1.D12/MISO, U2.DO
  5V: Part1.5V, Part2.5V
  N8: Part1.A5, Part2.SCL
  N9: Part1.A4, Part2.SDA
  N10: Part1.D13/SCK, U2.SCK
